// Logisim project 16bit computer.circ as structural Verilog: 8 circuits, main circuit main
module main (
  input  in_1
);

  wire and_1_out, and_2_out, and_3_out, and_4_out, and_5_out, and_6_out, clock_1_out, comparator_1_eq,
       comparator_1_gt, comparator_1_lt, d_ff_1_q, display_controller_1_hex_on, display_controller_1_neg_on,
       display_controller_1_negative, not_1_out, not_2_out, not_3_out, not_4_out, not_5_out, not_6_out,
       not_7_out, not_8_out, not_9_out, not_10_out, or_1_out, or_2_out, or_3_out, or_4_out,
       pull_resistor_1_node, rom_controller_1_jmp, rom_controller_1_select, step_reset_1_out_2;
  wire [3:0] display_controller_1_hundreds, display_controller_1_tens, display_controller_1_tenthousands,
       display_controller_1_thousands, display_controller_1_units;
  wire [6:0] ascii_1_ascii_out, bitselector_2_out, MA_q, rom_1_data, splitter_1_rest;
  wire [7:0] bitselector_1_out, bitselector_3_out, controlled_buffer_3_out, controlled_buffer_14_out, I_q,
       PC_q, SP_q;
  wire [7:7] MA_q_2;
  wire [10:0] counter_1_q;
  wire [15:0] A_q, adder_1_out, B_q, bitselector_4_out, controlled_buffer_2_out, controlled_buffer_4_out,
       controlled_buffer_6_out, controlled_buffer_8_out, controlled_buffer_11_out, controlled_buffer_13_out,
       OUT_q, ram_1_data, register_1_q;
  wire [16:0] splitter_1_out;
  wire [24:0] rom_2_data;

  LED led_1 (.in(MA_q[6]));
  LED led_2 (.in(MA_q_2[7]));
  LED led_3 (.in(MA_q[5]));
  LED led_4 (.in(counter_1_q[10]));
  LED led_5 (.in(counter_1_q[8]));
  LED led_6 (.in(counter_1_q[9]));
  not not_1 (not_1_out, and_6_out);
  and and_1 (and_1_out, counter_1_q[5], comparator_1_lt);
  and and_2 (and_2_out, counter_1_q[4], comparator_1_eq);
  or or_1 (or_1_out, and_1_out, and_2_out, and_3_out);
  LED led_7 (.in(MA_q[1]));
  LED led_8 (.in(MA_q[2]));
  LED led_9 (.in(MA_q[3]));
  LED led_10 (.in(MA_q[4]));
  LED led_11 (.in(counter_1_q[7]));
  LED led_12 (.in(counter_1_q[6]));
  LED led_13 (.in(counter_1_q[5]));
  LED led_14 (.in(counter_1_q[4]));
  and and_3 (and_3_out, counter_1_q[3], comparator_1_gt);
  Pull_Resistor pull_resistor_1 (.node(pull_resistor_1_node));
  assign pull_resistor_1_node = splitter_1_out[16] ? or_1_out : 1'bz;  // Controlled_Buffer controlled_buffer_1
  LED led_15 (.in(MA_q[0]));
  LED led_16 (.in(ram_1_data[14]));
  LED led_17 (.in(ram_1_data[15]));
  LED led_18 (.in(counter_1_q[3]));
  LED led_19 (.in(I_q[6]));
  LED led_20 (.in(I_q[7]));
  LED led_21 (.in(I_q[5]));
  not not_2 (not_2_out, rom_controller_1_jmp);
  D_Flip_Flop d_ff_1 (
    .clk(and_6_out), .D(pull_resistor_1_node), .Q(d_ff_1_q), .reset(and_4_out));  // open: Qn, preset, en
  and and_4 (and_4_out, and_6_out, not_3_out);
  not not_3 (not_3_out, splitter_1_out[16]);
  not not_4 (not_4_out, and_6_out);
  LED led_22 (.in(ram_1_data[12]));
  LED led_23 (.in(ram_1_data[10]));
  LED led_24 (.in(ram_1_data[11]));
  LED led_25 (.in(ram_1_data[13]));
  not not_5 (not_5_out, MA_q_2[7]);
  LED led_26 (.in(I_q[2]));
  LED led_27 (.in(I_q[4]));
  LED led_28 (.in(I_q[3]));
  LED led_29 (.in(I_q[1]));
  LED led_30 (.in(counter_1_q[0]));
  LED led_31 (.in(counter_1_q[1]));
  LED led_32 (.in(counter_1_q[2]));
  Counter #(.width(3), .max('h7)) counter_1 (
    .load(rom_controller_1_jmp), .D(3'b001), .count(not_2_out), .Q(counter_1_q[2:0]), .clk(not_1_out),
    .clr(step_reset_1_out_2));  // open: carry
  Step_reset step_reset_1 (.in_1(rom_2_data), .out_2(step_reset_1_out_2));
  ASCII ascii_1 (
    .INPUT(I_q), .ASCII_OUT(ascii_1_ascii_out), .CLK(and_6_out), .ASCII_IN(rom_1_data),
    .NORMAL(bitselector_2_out), .DEBUG(in_1));
  TTY tty_1 (.data(ascii_1_ascii_out), .clk(and_6_out), .we(or_2_out), .clr(splitter_1_rest[2]));
  or or_2 (or_2_out, in_1, splitter_1_rest[3]);
  LED led_33 (.in(ram_1_data[6]));
  LED led_34 (.in(ram_1_data[8]));
  LED led_35 (.in(ram_1_data[7]));
  LED led_36 (.in(ram_1_data[9]));
  RAM #(.addrWidth(7), .dataWidth(16), .bus("separate")) ram_1 (
    .addr(MA_q), .data(ram_1_data), .str(splitter_1_out[2]), .sel(not_5_out), .clk(and_6_out));  // open: din, ld, clr
  LED led_37 (.in(I_q[0]));
  ROM #(.addrWidth(11), .dataWidth(7)) rom_1 (.addr(counter_1_q), .data(rom_1_data), .sel(rom_controller_1_select));
  LED led_38 (.in(ram_1_data[3]));
  LED led_39 (.in(ram_1_data[4]));
  LED led_40 (.in(ram_1_data[5]));
  LED led_41 (.in(ram_1_data[2]));
  not not_6 (not_6_out, rom_controller_1_select);
  ROM_controller rom_controller_1 (
    .EN(in_1), .INSTRUCTION(rom_2_data), .JMP(rom_controller_1_jmp), .CLK(not_4_out),
    .SELECT(rom_controller_1_select), .ASCII_IN(rom_1_data));
  LED led_42 (.in(controlled_buffer_4_out[15]));
  LED led_43 (.in(controlled_buffer_4_out[14]));
  LED led_44 (.in(controlled_buffer_4_out[13]));
  LED led_45 (.in(ram_1_data[1]));
  LED led_46 (.in(ram_1_data[0]));
  RAM #(.addrWidth(7), .dataWidth(16), .bus("separate")) ram_2 (
    .addr(MA_q), .din(controlled_buffer_4_out), .data(ram_1_data), .str(splitter_1_out[2]), .sel(MA_q_2[7]),
    .clk(and_6_out));  // open: ld, clr
  assign controlled_buffer_2_out = splitter_1_out[4] ? controlled_buffer_4_out : 16'bz;  // Controlled_Buffer controlled_buffer_2
  Register #(.width(16)) I (
    .D(controlled_buffer_2_out), .Q({counter_1_q[10:3], I_q}), .clk(and_6_out));  // open: en, clr
  ROM #(.addrWidth(11), .dataWidth(25)) rom_2 (.addr(counter_1_q), .data(rom_2_data), .sel(not_6_out));
  Comparator #(.width(16), .mode("unsigned")) comparator_1 (
    .a(A_q), .b(controlled_buffer_4_out), .gt(comparator_1_gt), .eq(comparator_1_eq), .lt(comparator_1_lt));
  LED led_47 (.in(controlled_buffer_4_out[11]));
  LED led_48 (.in(controlled_buffer_4_out[9]));
  LED led_49 (.in(controlled_buffer_4_out[12]));
  LED led_50 (.in(controlled_buffer_4_out[10]));
  Register MA (.D(controlled_buffer_3_out), .Q({MA_q_2[7], MA_q}), .clk(and_6_out));  // open: en, clr
  assign controlled_buffer_3_out = splitter_1_out[5] ? bitselector_1_out : 8'bz;  // Controlled_Buffer controlled_buffer_3
  BitSelector #(.width(16), .group(8)) bitselector_1 (
    .in(controlled_buffer_4_out), .out(bitselector_1_out), .sel(1'b0));
  assign controlled_buffer_4_out = splitter_1_out[1] ? ram_1_data : 16'bz;  // Controlled_Buffer controlled_buffer_4
  assign controlled_buffer_4_out = splitter_1_out[3] ? {counter_1_q[10:3], I_q} : 16'bz;  // Controlled_Buffer controlled_buffer_5
  BitSelector #(.width(16), .group(7)) bitselector_2 (
    .in(controlled_buffer_4_out), .out(bitselector_2_out), .sel(2'b00));
  LED led_51 (.in(splitter_1_rest[5]));
  LED led_52 (.in(splitter_1_rest[6]));
  Splitter splitter_1 (.IN(rom_2_data), .OUT(splitter_1_out), .REST(splitter_1_rest));
  LED led_53 (.in(controlled_buffer_4_out[5]));
  LED led_54 (.in(controlled_buffer_4_out[8]));
  LED led_55 (.in(controlled_buffer_4_out[7]));
  LED led_56 (.in(controlled_buffer_4_out[6]));
  BitSelector #(.width(16), .group(8)) bitselector_3 (
    .in(controlled_buffer_4_out), .out(bitselector_3_out), .sel(1'b0));
  assign controlled_buffer_6_out = splitter_1_out[15] ? controlled_buffer_4_out : 16'bz;  // Controlled_Buffer controlled_buffer_6
  LED led_57 (.in(splitter_1_rest[3]));
  LED led_58 (.in(splitter_1_rest[2]));
  LED led_59 (.in(splitter_1_rest[4]));
  LED led_60 (.in(splitter_1_rest[1]));
  LED led_61 (.in(controlled_buffer_4_out[1]));
  LED led_62 (.in(controlled_buffer_4_out[4]));
  LED led_63 (.in(controlled_buffer_4_out[2]));
  LED led_64 (.in(controlled_buffer_4_out[3]));
  assign controlled_buffer_4_out = or_3_out ? bitselector_4_out : 16'bz;  // Controlled_Buffer controlled_buffer_7
  or or_3 (or_3_out, splitter_1_out[7], splitter_1_rest[4]);
  Register #(.width(16)) A (.D(controlled_buffer_8_out), .Q(A_q), .clk(and_6_out));  // open: en, clr
  assign controlled_buffer_8_out = splitter_1_out[10] ? controlled_buffer_4_out : 16'bz;  // Controlled_Buffer controlled_buffer_8
  assign controlled_buffer_4_out = splitter_1_out[11] ? register_1_q : 16'bz;  // Controlled_Buffer controlled_buffer_9
  assign controlled_buffer_4_out = splitter_1_out[13] ? B_q : 16'bz;  // Controlled_Buffer controlled_buffer_10
  assign controlled_buffer_11_out = splitter_1_out[14] ? controlled_buffer_4_out : 16'bz;  // Controlled_Buffer controlled_buffer_11
  LED led_65 (.in(splitter_1_out[14]));
  LED led_66 (.in(splitter_1_out[15]));
  LED led_67 (.in(splitter_1_rest[0]));
  LED led_68 (.in(splitter_1_out[16]));
  LED led_69 (.in(controlled_buffer_4_out[0]));
  BitSelector #(.group(16)) bitselector_4 (.in(controlled_buffer_14_out), .out(bitselector_4_out), .sel(1'b0));
  Counter PC (
    .load(splitter_1_out[6]), .D(bitselector_3_out), .count(not_7_out), .Q(PC_q), .clk(and_5_out));  // open: carry, clr
  not not_7 (not_7_out, splitter_1_out[6]);
  and and_5 (and_5_out, and_6_out, or_4_out);
  or or_4 (or_4_out, d_ff_1_q, splitter_1_out[8]);
  assign controlled_buffer_4_out = splitter_1_out[9] ? A_q : 16'bz;  // Controlled_Buffer controlled_buffer_12
  Adder #(.width(16)) adder_1 (
    .a(A_q), .b(controlled_buffer_13_out), .out(adder_1_out), .cin(splitter_1_out[12]));  // open: cout
  Register #(.width(16)) register_1 (.D(adder_1_out), .Q(register_1_q), .clk(not_9_out));  // open: en, clr
  assign controlled_buffer_13_out = not_8_out ? B_q : 16'bz;  // Controlled_Buffer controlled_buffer_13
  assign controlled_buffer_13_out = splitter_1_out[12] ? ~B_q : 16'bz;  // Controlled_Inverter controlled_inverter_1
  not not_8 (not_8_out, splitter_1_out[12]);
  Register #(.width(16)) B (.D(controlled_buffer_11_out), .Q(B_q), .clk(and_6_out));  // open: en, clr
  Register #(.width(16)) OUT (.D(controlled_buffer_6_out), .Q(OUT_q), .clk(and_6_out));  // open: en, clr
  LED led_70 (.in(splitter_1_out[12]));
  LED led_71 (.in(splitter_1_out[13]));
  LED led_72 (.in(splitter_1_out[10]));
  LED led_73 (.in(splitter_1_out[11]));
  assign controlled_buffer_14_out = splitter_1_out[7] ? PC_q : 8'bz;  // Controlled_Buffer controlled_buffer_14
  LED led_74 (.in(PC_q[7]));
  LED led_75 (.in(PC_q[6]));
  LED led_76 (.in(A_q[14]));
  LED led_77 (.in(A_q[15]));
  LED led_78 (.in(A_q[12]));
  LED led_79 (.in(A_q[13]));
  LED led_80 (.in(register_1_q[12]));
  LED led_81 (.in(register_1_q[15]));
  LED led_82 (.in(register_1_q[14]));
  LED led_83 (.in(register_1_q[13]));
  not not_9 (not_9_out, and_6_out);
  LED led_84 (.in(B_q[15]));
  LED led_85 (.in(B_q[13]));
  LED led_86 (.in(B_q[12]));
  LED led_87 (.in(B_q[14]));
  LED HEX (.in(display_controller_1_hex_on));
  LED _2c (.in(display_controller_1_neg_on));
  Display_controller display_controller_1 (
    .NEGMODE(splitter_1_rest[0]), .INPUT(OUT_q), .HEXMODE(splitter_1_rest[1]),
    .NEGATIVE(display_controller_1_negative), .UNITS(display_controller_1_units),
    .TENS(display_controller_1_tens), .HUNDREDS(display_controller_1_hundreds),
    .THOUSANDS(display_controller_1_thousands), .TENTHOUSANDS(display_controller_1_tenthousands),
    .HEX_ON(display_controller_1_hex_on), .NEG_ON(display_controller_1_neg_on));
  LED led_88 (.in(splitter_1_out[6]));
  LED led_89 (.in(splitter_1_out[9]));
  LED led_90 (.in(splitter_1_out[7]));
  LED led_91 (.in(splitter_1_out[8]));
  LED led_92 (.in(PC_q[3]));
  LED led_93 (.in(PC_q[4]));
  LED led_94 (.in(PC_q[5]));
  LED led_95 (.in(PC_q[2]));
  LED led_96 (.in(A_q[11]));
  LED led_97 (.in(A_q[8]));
  LED led_98 (.in(A_q[10]));
  LED led_99 (.in(A_q[9]));
  LED led_100 (.in(register_1_q[8]));
  LED led_101 (.in(register_1_q[10]));
  LED led_102 (.in(register_1_q[9]));
  LED led_103 (.in(register_1_q[11]));
  LED led_104 (.in(B_q[11]));
  LED led_105 (.in(B_q[8]));
  LED led_106 (.in(B_q[10]));
  LED led_107 (.in(B_q[9]));
  _7_Segment_Display u_7_segment_display_1 (.g(display_controller_1_negative));  // open: f, a, b, e, d, c, dp
  Hex_Digit_Display hex_digit_display_1 (.value(display_controller_1_tenthousands));  // open: dp
  LED led_108 (.in(splitter_1_out[3]));
  LED led_109 (.in(splitter_1_out[2]));
  LED led_110 (.in(splitter_1_out[5]));
  LED led_111 (.in(splitter_1_out[4]));
  assign controlled_buffer_14_out = splitter_1_rest[4] ? SP_q : 8'bz;  // Controlled_Buffer controlled_buffer_15
  LED led_112 (.in(PC_q[1]));
  LED led_113 (.in(PC_q[0]));
  LED led_114 (.in(A_q[5]));
  LED led_115 (.in(A_q[7]));
  LED led_116 (.in(A_q[4]));
  LED led_117 (.in(A_q[6]));
  LED led_118 (.in(register_1_q[4]));
  LED led_119 (.in(register_1_q[5]));
  LED led_120 (.in(register_1_q[6]));
  LED led_121 (.in(register_1_q[7]));
  LED led_122 (.in(B_q[6]));
  LED led_123 (.in(B_q[5]));
  LED led_124 (.in(B_q[7]));
  LED led_125 (.in(B_q[4]));
  Hex_Digit_Display hex_digit_display_2 (.value(display_controller_1_thousands));  // open: dp
  Hex_Digit_Display hex_digit_display_3 (.value(display_controller_1_hundreds));  // open: dp
  LED led_126 (.in(splitter_1_out[1]));
  LED led_127 (.in(splitter_1_out[0]));
  LED led_128 (.in(A_q[2]));
  LED led_129 (.in(A_q[3]));
  LED led_130 (.in(A_q[0]));
  LED led_131 (.in(A_q[1]));
  LED led_132 (.in(register_1_q[1]));
  LED led_133 (.in(register_1_q[3]));
  LED led_134 (.in(register_1_q[2]));
  LED led_135 (.in(register_1_q[0]));
  LED led_136 (.in(B_q[3]));
  LED led_137 (.in(B_q[2]));
  LED led_138 (.in(B_q[0]));
  LED led_139 (.in(B_q[1]));
  Hex_Digit_Display hex_digit_display_4 (.value(display_controller_1_tens));  // open: dp
  Hex_Digit_Display hex_digit_display_5 (.value(display_controller_1_units));  // open: dp
  Counter #(.max('h8f)) SP (
    .load(splitter_1_rest[6]), .count(splitter_1_rest[5]), .Q(SP_q), .clk(and_6_out));  // open: D, carry, clr
  and and_6 (and_6_out, not_10_out, clock_1_out);
  not not_10 (not_10_out, splitter_1_out[0]);
  Clock clock_1 (.out(clock_1_out));

  // Notes on the sheet:
  //   contents of rom_1 (hex, n*v repeats v):
  //   47 45 54 d 4*0 4c 44 41 20 7f 7f d 0 4c 44 42 20 7f 7f d 0 53 54 41 20 7f 7f d 0 53 54 42 20 7f 7f d
  //   0 41 44 44 d 4*0 53 55 42 d 4*0 4f 55 54 d 4*0 4a 4d 50 20 7f 7f d 0 4a 47 54 20 7f 7f d 0 4a 45 51
  //   20 7f 7f d 0 4a 4c 54 20 7f 7f d 0 4f 48 45 d 4*0 4f 4e 45 d 4*0 52 53 54 d 4*0 48 4c 54 d 4*0 50 52
  //   54 d 4*0 43 2c 52 d
  //   contents of rom_2 (hex, n*v repeats v):
  //   1000000 a0 112 5*0 1000000 a0 112 28 402 0 0 0 1000000 a0 112 28 4002 0 0 0 1000000 a0 112 28 204 0
  //   0 0 1000000 a0 112 28 2004 0 0 0 1000000 a0 112 28 4002 c00 0 0 1000000 a0 112 28 5002 1c00 0 0
  //   1000000 a0 112 8200 4*0 1000000 a0 112 148 4*0 1000000 a0 112 12000 48 0 0 0 1000000 a0 112 12000 48
  //   0 0 0 1000000 a0 112 40000 4*0 1000000 a0 112 12000 48 0 0 0 1000000 a0 112 20000 4*0 1000000 a0 112
  //   c560 4*0 1000000 a0 112 1 4*0 1000000 a0 112 100008 4*0 1000000 a0 112 80000 4*0 1000000 a0 112
  //   c00000 200020 204 0 0 1000000 a0 112 200020 402 400000 0 0 1000000 a0 112 c00000 200020 84 148 0
  //   1000000 a0 112 200020 400142
  //   SD
  //   SE
  //   SO
  //   CT
  //   ON
  //   PT
  //   OH
  //   CP
  //   OI
  //   BI
  //   AI
  //   SU
  //   BO
  //   EO
  //   J
  //   CO
  //   CE
  //   AO
  //   IO
  //   MI
  //   RI
  //   II
  //   H
  //   RO
endmodule

module Step_reset (
  input  [24:0] in_1,
  output out_2
);

  wire not_1_out, not_2_out, not_3_out, not_4_out, not_5_out, not_6_out, not_7_out, not_8_out, not_9_out,
       not_10_out, not_11_out, not_12_out, not_13_out, not_14_out, not_15_out, not_16_out, not_17_out,
       not_18_out, not_19_out, not_20_out, not_21_out, not_22_out, not_23_out, not_24_out, not_25_out;

  not not_1 (not_1_out, in_1[0]);
  not not_2 (not_2_out, in_1[1]);
  not not_3 (not_3_out, in_1[2]);
  not not_4 (not_4_out, in_1[3]);
  not not_5 (not_5_out, in_1[4]);
  not not_6 (not_6_out, in_1[5]);
  not not_7 (not_7_out, in_1[6]);
  not not_8 (not_8_out, in_1[7]);
  not not_9 (not_9_out, in_1[8]);
  not not_10 (not_10_out, in_1[9]);
  not not_11 (not_11_out, in_1[10]);
  not not_12 (not_12_out, in_1[11]);
  not not_13 (not_13_out, in_1[12]);
  not not_14 (not_14_out, in_1[13]);
  not not_15 (not_15_out, in_1[14]);
  not not_16 (not_16_out, in_1[15]);
  not not_17 (not_17_out, in_1[16]);
  not not_18 (not_18_out, in_1[17]);
  not not_19 (not_19_out, in_1[18]);
  not not_20 (not_20_out, in_1[19]);
  not not_21 (not_21_out, in_1[20]);
  not not_22 (not_22_out, in_1[21]);
  not not_23 (not_23_out, in_1[22]);
  not not_24 (not_24_out, in_1[23]);
  not not_25 (not_25_out, in_1[24]);
  and and_1 (out_2, not_1_out, not_2_out, not_3_out, not_4_out, not_5_out, not_6_out, not_7_out, not_8_out, not_9_out, not_10_out, not_11_out, not_12_out, not_13_out, not_14_out, not_15_out, not_16_out, not_17_out, not_18_out, not_19_out, not_20_out, not_21_out, not_22_out, not_23_out, not_24_out, not_25_out);
endmodule

module ADD3 (
  input  A3,
  input  A2,
  input  A1,
  input  A0,
  output S3,
  output S2,
  output S1,
  output S0
);

  wire and_1_out, and_2_out, and_3_out, and_4_out, and_5_out, and_6_out, and_7_out, and_8_out, and_9_out,
       and_10_out, not_1_out, not_2_out, not_3_out, not_4_out, not_5_out, not_6_out, not_7_out, not_8_out;

  and and_1 (and_1_out, A2, A0);
  and and_2 (and_2_out, A2, A1);
  and and_3 (and_3_out, A2, not_1_out, not_2_out);
  not not_1 (not_1_out, A1);
  not not_2 (not_2_out, A0);
  and and_4 (and_4_out, A3, A0);
  not not_3 (not_3_out, A2);
  and and_5 (and_5_out, not_3_out, A1);
  and and_6 (and_6_out, A1, A0);
  and and_7 (and_7_out, A3, not_4_out);
  not not_4 (not_4_out, A0);
  not not_5 (not_5_out, A3);
  and and_8 (and_8_out, not_5_out, not_6_out, A0);
  not not_6 (not_6_out, A2);
  and and_9 (and_9_out, A2, A1, not_7_out);
  not not_7 (not_7_out, A0);
  and and_10 (and_10_out, A3, not_8_out);
  not not_8 (not_8_out, A0);
  or or_1 (S3, and_1_out, and_2_out, A3);
  or or_2 (S2, and_3_out, and_4_out);
  or or_3 (S1, and_5_out, and_6_out, and_7_out);
  or or_4 (S0, and_8_out, and_9_out, and_10_out);
endmodule

module Binary_to_BCD (
  input  [15:0] in_1,
  input  in_2,
  output [3:0] UNITS,
  output [3:0] TENS,
  output [3:0] HUNDREDS,
  output [3:0] THOUSANDS,
  output [3:0] TENTHOUSANDS,
  output NEGATIVE
);

  wire add3_1_s0, add3_1_s1, add3_1_s2, add3_1_s3, add3_2_s0, add3_2_s1, add3_2_s2, add3_2_s3, add3_3_s0,
       add3_3_s1, add3_3_s2, add3_3_s3, add3_4_s0, add3_4_s1, add3_4_s2, add3_4_s3, add3_5_s0, add3_5_s1,
       add3_5_s2, add3_5_s3, add3_6_s0, add3_6_s1, add3_6_s2, add3_6_s3, add3_7_s0, add3_7_s1, add3_7_s2,
       add3_7_s3, add3_8_s0, add3_8_s1, add3_8_s2, add3_8_s3, add3_9_s0, add3_9_s1, add3_9_s2, add3_9_s3,
       add3_10_s0, add3_10_s1, add3_10_s2, add3_10_s3, add3_11_s0, add3_11_s1, add3_11_s2, add3_11_s3,
       add3_12_s0, add3_12_s1, add3_12_s2, add3_12_s3, add3_13_s0, add3_13_s1, add3_13_s2, add3_13_s3,
       add3_14_s0, add3_14_s1, add3_14_s2, add3_14_s3, add3_15_s0, add3_15_s1, add3_15_s2, add3_15_s3,
       add3_16_s0, add3_16_s1, add3_16_s2, add3_16_s3, add3_17_s0, add3_17_s1, add3_17_s2, add3_17_s3,
       add3_18_s0, add3_18_s1, add3_18_s2, add3_18_s3, add3_19_s0, add3_19_s1, add3_19_s2, add3_19_s3,
       add3_20_s0, add3_20_s1, add3_20_s2, add3_20_s3, add3_21_s0, add3_21_s1, add3_21_s2, add3_21_s3,
       add3_22_s0, add3_22_s1, add3_22_s2, add3_22_s3, add3_23_s0, add3_23_s1, add3_23_s2, add3_23_s3,
       add3_24_s0, add3_24_s1, add3_24_s2, add3_24_s3, add3_25_s0, add3_25_s1, add3_25_s2, add3_25_s3,
       add3_26_s0, add3_26_s1, add3_26_s2, add3_26_s3, add3_27_s0, add3_27_s1, add3_27_s2, add3_28_s0,
       add3_28_s1, add3_28_s2, add3_30_s0, add3_30_s1, add3_30_s2, add3_30_s3, add3_32_s0, add3_32_s1,
       add3_32_s2, add3_32_s3, add3_34_s0, add3_34_s1, add3_34_s2, add3_34_s3, add3_36_s0, add3_36_s1,
       add3_36_s2, and_2_out, not_2_out, not_3_out, pull_resistor_1_node;
  wire [14:0] not_1_out, subtractor_1_out;
  wire [14:1] controlled_buffer_1_out;

  assign not_1_out = ~subtractor_1_out;  // NOT_Gate not_1, 15 bits wide
  assign {controlled_buffer_1_out, UNITS[0]} = NEGATIVE ? not_1_out : 15'bz;  // Controlled_Buffer controlled_buffer_1
  Subtractor #(.width(15)) subtractor_1 (.a(in_1[14:0]), .b(15'h1), .out(subtractor_1_out));  // open: bin, bout
  and and_1 (NEGATIVE, in_1[15], in_2);
  and and_2 (and_2_out, in_1[15], not_2_out);
  not not_2 (not_2_out, in_2);
  assign {controlled_buffer_1_out, UNITS[0]} = not_3_out ? in_1[14:0] : 15'bz;  // Controlled_Buffer controlled_buffer_2
  not not_3 (not_3_out, NEGATIVE);
  ADD3 add3_1 (
    .A3(pull_resistor_1_node), .A2(and_2_out), .A1(controlled_buffer_1_out[14]),
    .A0(controlled_buffer_1_out[13]), .S3(add3_1_s3), .S2(add3_1_s2), .S1(add3_1_s1), .S0(add3_1_s0));
  Pull_Resistor pull_resistor_1 (.node(pull_resistor_1_node));
  ADD3 add3_2 (
    .A3(add3_3_s2), .A2(add3_3_s1), .A1(add3_3_s0), .A0(controlled_buffer_1_out[11]), .S3(add3_2_s3),
    .S2(add3_2_s2), .S1(add3_2_s1), .S0(add3_2_s0));
  ADD3 add3_3 (
    .A3(add3_1_s2), .A2(add3_1_s1), .A1(add3_1_s0), .A0(controlled_buffer_1_out[12]), .S3(add3_3_s3),
    .S2(add3_3_s2), .S1(add3_3_s1), .S0(add3_3_s0));
  ADD3 add3_4 (
    .A3(pull_resistor_1_node), .A2(pull_resistor_1_node), .A1(add3_1_s3), .A0(add3_3_s3), .S3(add3_4_s3),
    .S2(add3_4_s2), .S1(add3_4_s1), .S0(add3_4_s0));
  ADD3 add3_5 (
    .A3(add3_6_s2), .A2(add3_6_s1), .A1(add3_6_s0), .A0(controlled_buffer_1_out[9]), .S3(add3_5_s3),
    .S2(add3_5_s2), .S1(add3_5_s1), .S0(add3_5_s0));
  ADD3 add3_6 (
    .A3(add3_2_s2), .A2(add3_2_s1), .A1(add3_2_s0), .A0(controlled_buffer_1_out[10]), .S3(add3_6_s3),
    .S2(add3_6_s2), .S1(add3_6_s1), .S0(add3_6_s0));
  ADD3 add3_7 (
    .A3(add3_8_s2), .A2(add3_8_s1), .A1(add3_8_s0), .A0(add3_6_s3), .S3(add3_7_s3), .S2(add3_7_s2),
    .S1(add3_7_s1), .S0(add3_7_s0));
  ADD3 add3_8 (
    .A3(add3_4_s2), .A2(add3_4_s1), .A1(add3_4_s0), .A0(add3_2_s3), .S3(add3_8_s3), .S2(add3_8_s2),
    .S1(add3_8_s1), .S0(add3_8_s0));
  ADD3 add3_9 (
    .A3(add3_10_s2), .A2(add3_10_s1), .A1(add3_10_s0), .A0(controlled_buffer_1_out[7]), .S3(add3_9_s3),
    .S2(add3_9_s2), .S1(add3_9_s1), .S0(add3_9_s0));
  ADD3 add3_10 (
    .A3(add3_5_s2), .A2(add3_5_s1), .A1(add3_5_s0), .A0(controlled_buffer_1_out[8]), .S3(add3_10_s3),
    .S2(add3_10_s2), .S1(add3_10_s1), .S0(add3_10_s0));
  ADD3 add3_11 (
    .A3(add3_12_s2), .A2(add3_12_s1), .A1(add3_12_s0), .A0(add3_10_s3), .S3(add3_11_s3), .S2(add3_11_s2),
    .S1(add3_11_s1), .S0(add3_11_s0));
  ADD3 add3_12 (
    .A3(add3_7_s2), .A2(add3_7_s1), .A1(add3_7_s0), .A0(add3_5_s3), .S3(add3_12_s3), .S2(add3_12_s2),
    .S1(add3_12_s1), .S0(add3_12_s0));
  ADD3 add3_13 (
    .A3(add3_14_s2), .A2(add3_14_s1), .A1(add3_14_s0), .A0(add3_12_s3), .S3(add3_13_s3), .S2(add3_13_s2),
    .S1(add3_13_s1), .S0(add3_13_s0));
  ADD3 add3_14 (
    .A3(add3_4_s3), .A2(add3_4_s3), .A1(add3_8_s3), .A0(add3_7_s3), .S3(add3_14_s3), .S2(add3_14_s2),
    .S1(add3_14_s1), .S0(add3_14_s0));
  ADD3 add3_15 (
    .A3(add3_16_s2), .A2(add3_16_s1), .A1(add3_16_s0), .A0(controlled_buffer_1_out[5]), .S3(add3_15_s3),
    .S2(add3_15_s2), .S1(add3_15_s1), .S0(add3_15_s0));
  ADD3 add3_16 (
    .A3(add3_9_s2), .A2(add3_9_s1), .A1(add3_9_s0), .A0(controlled_buffer_1_out[6]), .S3(add3_16_s3),
    .S2(add3_16_s2), .S1(add3_16_s1), .S0(add3_16_s0));
  ADD3 add3_17 (
    .A3(add3_18_s2), .A2(add3_18_s1), .A1(add3_18_s0), .A0(add3_16_s3), .S3(add3_17_s3), .S2(add3_17_s2),
    .S1(add3_17_s1), .S0(add3_17_s0));
  ADD3 add3_18 (
    .A3(add3_11_s2), .A2(add3_11_s1), .A1(add3_11_s0), .A0(add3_9_s3), .S3(add3_18_s3), .S2(add3_18_s2),
    .S1(add3_18_s1), .S0(add3_18_s0));
  ADD3 add3_19 (
    .A3(add3_20_s2), .A2(add3_20_s1), .A1(add3_20_s0), .A0(add3_18_s3), .S3(add3_19_s3), .S2(add3_19_s2),
    .S1(add3_19_s1), .S0(add3_19_s0));
  ADD3 add3_20 (
    .A3(add3_13_s2), .A2(add3_13_s1), .A1(add3_13_s0), .A0(add3_11_s3), .S3(add3_20_s3), .S2(add3_20_s2),
    .S1(add3_20_s1), .S0(add3_20_s0));
  ADD3 add3_21 (
    .A3(add3_22_s2), .A2(add3_22_s1), .A1(add3_22_s0), .A0(controlled_buffer_1_out[3]), .S3(add3_21_s3),
    .S2(add3_21_s2), .S1(add3_21_s1), .S0(add3_21_s0));
  ADD3 add3_22 (
    .A3(add3_15_s2), .A2(add3_15_s1), .A1(add3_15_s0), .A0(controlled_buffer_1_out[4]), .S3(add3_22_s3),
    .S2(add3_22_s2), .S1(add3_22_s1), .S0(add3_22_s0));
  ADD3 add3_23 (
    .A3(add3_24_s2), .A2(add3_24_s1), .A1(add3_24_s0), .A0(add3_22_s3), .S3(add3_23_s3), .S2(add3_23_s2),
    .S1(add3_23_s1), .S0(add3_23_s0));
  ADD3 add3_24 (
    .A3(add3_17_s2), .A2(add3_17_s1), .A1(add3_17_s0), .A0(add3_15_s3), .S3(add3_24_s3), .S2(add3_24_s2),
    .S1(add3_24_s1), .S0(add3_24_s0));
  ADD3 add3_25 (
    .A3(add3_26_s2), .A2(add3_26_s1), .A1(add3_26_s0), .A0(add3_24_s3), .S3(add3_25_s3), .S2(add3_25_s2),
    .S1(add3_25_s1), .S0(add3_25_s0));
  ADD3 add3_26 (
    .A3(add3_19_s2), .A2(add3_19_s1), .A1(add3_19_s0), .A0(add3_17_s3), .S3(add3_26_s3), .S2(add3_26_s2),
    .S1(add3_26_s1), .S0(add3_26_s0));
  ADD3 add3_27 (
    .A3(add3_28_s2), .A2(add3_28_s1), .A1(add3_28_s0), .A0(add3_26_s3), .S3(TENTHOUSANDS[2]),
    .S2(add3_27_s2), .S1(add3_27_s1), .S0(add3_27_s0));
  ADD3 add3_28 (
    .A3(add3_14_s3), .A2(add3_13_s3), .A1(add3_20_s3), .A0(add3_19_s3), .S3(TENTHOUSANDS[3]),
    .S2(add3_28_s2), .S1(add3_28_s1), .S0(add3_28_s0));
  ADD3 add3_29 (
    .A3(add3_30_s2), .A2(add3_30_s1), .A1(add3_30_s0), .A0(controlled_buffer_1_out[1]), .S3(TENS[0]),
    .S2(UNITS[3]), .S1(UNITS[2]), .S0(UNITS[1]));
  ADD3 add3_30 (
    .A3(add3_21_s2), .A2(add3_21_s1), .A1(add3_21_s0), .A0(controlled_buffer_1_out[2]), .S3(add3_30_s3),
    .S2(add3_30_s2), .S1(add3_30_s1), .S0(add3_30_s0));
  ADD3 add3_31 (
    .A3(add3_32_s2), .A2(add3_32_s1), .A1(add3_32_s0), .A0(add3_30_s3), .S3(HUNDREDS[0]), .S2(TENS[3]),
    .S1(TENS[2]), .S0(TENS[1]));
  ADD3 add3_32 (
    .A3(add3_23_s2), .A2(add3_23_s1), .A1(add3_23_s0), .A0(add3_21_s3), .S3(add3_32_s3), .S2(add3_32_s2),
    .S1(add3_32_s1), .S0(add3_32_s0));
  ADD3 add3_33 (
    .A3(add3_34_s2), .A2(add3_34_s1), .A1(add3_34_s0), .A0(add3_32_s3), .S3(THOUSANDS[0]), .S2(HUNDREDS[3]),
    .S1(HUNDREDS[2]), .S0(HUNDREDS[1]));
  ADD3 add3_34 (
    .A3(add3_25_s2), .A2(add3_25_s1), .A1(add3_25_s0), .A0(add3_23_s3), .S3(add3_34_s3), .S2(add3_34_s2),
    .S1(add3_34_s1), .S0(add3_34_s0));
  ADD3 add3_35 (
    .A3(add3_36_s2), .A2(add3_36_s1), .A1(add3_36_s0), .A0(add3_34_s3), .S3(TENTHOUSANDS[0]),
    .S2(THOUSANDS[3]), .S1(THOUSANDS[2]), .S0(THOUSANDS[1]));
  ADD3 add3_36 (
    .A3(add3_27_s2), .A2(add3_27_s1), .A1(add3_27_s0), .A0(add3_25_s3), .S3(TENTHOUSANDS[1]),
    .S2(add3_36_s2), .S1(add3_36_s1), .S0(add3_36_s0));
endmodule

module Splitter (
  input  [24:0] IN,
  output [16:0] OUT,
  output [6:0] REST
);


  assign OUT = IN[16:0];
  assign REST = IN[23:17];

  // Notes on the sheet:
  //   IN: pull=down
endmodule

module Display_controller (
  input  NEGMODE,
  input  [15:0] INPUT,
  input  HEXMODE,
  output NEG_ON,
  output NEGATIVE,
  output [3:0] UNITS,
  output [3:0] TENS,
  output HEX_ON,
  output [3:0] HUNDREDS,
  output [3:0] THOUSANDS,
  output [3:0] TENTHOUSANDS
);

  wire d_ff_1_qn, d_ff_2_qn, not_1_out, not_2_out, not_3_out, not_4_out, not_5_out;
  wire [3:0] binary_to_bcd_1_hundreds, binary_to_bcd_1_tens, binary_to_bcd_1_tenthousands,
       binary_to_bcd_1_thousands, binary_to_bcd_1_units;

  D_Flip_Flop d_ff_1 (.clk(NEGMODE), .D(d_ff_1_qn), .Q(NEG_ON), .Qn(d_ff_1_qn));  // open: preset, en, reset
  D_Flip_Flop d_ff_2 (.clk(HEXMODE), .D(d_ff_2_qn), .Q(HEX_ON), .Qn(d_ff_2_qn));  // open: preset, en, reset
  Binary_to_BCD binary_to_bcd_1 (
    .in_1(INPUT), .UNITS(binary_to_bcd_1_units), .TENS(binary_to_bcd_1_tens),
    .HUNDREDS(binary_to_bcd_1_hundreds), .in_2(NEG_ON), .THOUSANDS(binary_to_bcd_1_thousands),
    .TENTHOUSANDS(binary_to_bcd_1_tenthousands), .NEGATIVE(NEGATIVE));
  assign UNITS = not_1_out ? binary_to_bcd_1_units : 4'bz;  // Controlled_Buffer controlled_buffer_1
  not not_1 (not_1_out, HEX_ON);
  assign UNITS = HEX_ON ? INPUT[3:0] : 4'bz;  // Controlled_Buffer controlled_buffer_2
  assign TENS = not_2_out ? binary_to_bcd_1_tens : 4'bz;  // Controlled_Buffer controlled_buffer_3
  not not_2 (not_2_out, HEX_ON);
  assign TENS = HEX_ON ? INPUT[7:4] : 4'bz;  // Controlled_Buffer controlled_buffer_4
  assign HUNDREDS = not_3_out ? binary_to_bcd_1_hundreds : 4'bz;  // Controlled_Buffer controlled_buffer_5
  not not_3 (not_3_out, HEX_ON);
  assign HUNDREDS = HEX_ON ? INPUT[11:8] : 4'bz;  // Controlled_Buffer controlled_buffer_6
  assign THOUSANDS = not_4_out ? binary_to_bcd_1_thousands : 4'bz;  // Controlled_Buffer controlled_buffer_7
  not not_4 (not_4_out, HEX_ON);
  assign THOUSANDS = HEX_ON ? INPUT[15:12] : 4'bz;  // Controlled_Buffer controlled_buffer_8
  assign TENTHOUSANDS = not_5_out ? binary_to_bcd_1_tenthousands : 4'bz;  // Controlled_Buffer controlled_buffer_9
  not not_5 (not_5_out, HEX_ON);
  assign TENTHOUSANDS = HEX_ON ? 4'b0000 : 4'bz;  // Controlled_Buffer controlled_buffer_10
endmodule

module ASCII (
  input  [7:0] INPUT,
  input  [6:0] NORMAL,
  input  DEBUG,
  input  CLK,
  input  [6:0] ASCII_IN,
  output [6:0] ASCII_OUT
);

  wire comparator_1_lt, comparator_2_eq, comparator_2_gt, comparator_2_lt, d_ff_1_qn, d_ff_2_q, not_1_out,
       not_2_out, or_1_out, pull_resistor_1_node;
  wire [6:0] adder_1_out, bitselector_1_out, bitselector_2_out, controlled_buffer_1_out,
       controlled_buffer_2_out, multiplexer_1_out, multiplexer_2_out, xor_1_out;
  wire [7:0] and_1_out, shifter_1_out;

  Shifter #(.shift("lr")) shifter_1 (.in(INPUT), .\dist (3'b100), .out(shifter_1_out));
  BitSelector #(.group(7)) bitselector_1 (.in(and_1_out), .out(bitselector_1_out), .sel(pull_resistor_1_node));
  assign and_1_out = INPUT & 8'hf;  // AND_Gate and_1, 8 bits wide
  Pull_Resistor pull_resistor_1 (.node(pull_resistor_1_node));
  D_Flip_Flop d_ff_1 (.clk(d_ff_2_q), .D(d_ff_1_qn), .Qn(d_ff_1_qn));  // open: Q, preset, en, reset
  BitSelector #(.group(7)) bitselector_2 (.in(shifter_1_out), .out(bitselector_2_out), .sel(pull_resistor_1_node));
  Multiplexer #(.width(7), .disabled(0), .enable("false")) multiplexer_1 (
    .in0(bitselector_2_out), .in1(bitselector_1_out), .out(multiplexer_1_out), .sel(not_1_out));
  not not_1 (not_1_out, d_ff_1_qn);
  D_Flip_Flop #(.trigger("falling")) d_ff_2 (
    .clk(CLK), .D(comparator_2_eq), .Q(d_ff_2_q), .reset(CLK));  // open: Qn, preset, en
  Comparator #(.width(7), .mode("unsigned")) comparator_1 (
    .a(7'b0001001), .b(multiplexer_1_out), .lt(comparator_1_lt));  // open: gt, eq
  Comparator #(.width(7)) comparator_2 (
    .a({7{1'b1}}), .b(ASCII_IN), .gt(comparator_2_gt), .eq(comparator_2_eq), .lt(comparator_2_lt));
  Multiplexer #(.width(7), .disabled(0), .enable("false")) multiplexer_2 (
    .in0(7'b0110000), .in1(7'b0110111), .out(multiplexer_2_out), .sel(comparator_1_lt));
  Adder #(.width(7)) adder_1 (.a(multiplexer_2_out), .b(multiplexer_1_out), .out(adder_1_out));  // open: cin, cout
  Pull_Resistor pull_resistor_2 (.node(comparator_2_gt));
  or or_1 (or_1_out, comparator_2_gt, comparator_2_lt);
  Pull_Resistor pull_resistor_3 (.node(comparator_2_lt));
  Pull_Resistor pull_resistor_4 (.node(comparator_2_eq));
  assign controlled_buffer_1_out = comparator_2_eq ? adder_1_out : 7'bz;  // Controlled_Buffer controlled_buffer_1
  Pull_Resistor pull_resistor_5 (.node(controlled_buffer_1_out));
  assign controlled_buffer_2_out = or_1_out ? ASCII_IN : 7'bz;  // Controlled_Buffer controlled_buffer_2
  Pull_Resistor pull_resistor_6 (.node(controlled_buffer_2_out));
  assign xor_1_out = controlled_buffer_1_out ^ controlled_buffer_2_out;  // XOR_Gate xor_1, 7 bits wide
  not not_2 (not_2_out, DEBUG);
  Multiplexer #(.width(7), .disabled(0), .enable("false")) multiplexer_3 (
    .in0(xor_1_out), .in1(NORMAL), .out(ASCII_OUT), .sel(not_2_out));
endmodule

module ROM_controller (
  input  [6:0] ASCII_IN,
  input  [24:0] INSTRUCTION,
  input  CLK,
  input  EN,
  output JMP,
  output SELECT
);

  wire comparator_1_eq, comparator_2_eq, d_ff_1_q, d_ff_2_q, d_ff_3_q, d_ff_3_qn, or_1_out;

  and and_1 (JMP, d_ff_2_q, ~CLK);  // AND_Gate
  and and_2 (SELECT, EN, d_ff_3_q);
  D_Flip_Flop d_ff_1 (.clk(CLK), .D(JMP), .Q(d_ff_1_q));  // open: Qn, preset, en, reset
  or or_1 (or_1_out, JMP, comparator_1_eq);
  Comparator #(.width(7)) comparator_1 (.a(ASCII_IN), .b(7'b0001101), .eq(comparator_1_eq));  // open: gt, lt
  D_Flip_Flop d_ff_2 (.clk(or_1_out), .D(comparator_1_eq), .Q(d_ff_2_q), .reset(d_ff_1_q));  // open: Qn, preset, en
  Comparator #(.width(25)) comparator_2 (.a(INSTRUCTION), .b(25'h1000000), .eq(comparator_2_eq));  // open: gt, lt
  D_Flip_Flop d_ff_3 (
    .clk(comparator_2_eq), .D(d_ff_3_qn), .Q(d_ff_3_q), .Qn(d_ff_3_qn), .reset(d_ff_1_q));  // open: preset, en

  // Notes on the sheet:
  //   INSTRUCTION: pull=down
endmodule
